# Fritzing sketch Brail Keyboard(Arduino) (saved by Fritzing 0.9.10b)
breadboards: 1

parts:
  TP1 = TTP223 Touch Module [part_number=TTP223]
  TP2 = TTP223 Touch Module [part_number=TTP223]
  TP3 = TTP223 Touch Module [part_number=TTP223]
  TP4 = TTP223 Touch Module [part_number=TTP223]
  TP5 = TTP223 Touch Module [part_number=TTP223]
  TP6 = TTP223 Touch Module [part_number=TTP223]
  Part1 = Arduino Uno (Rev3)
  Part2 = LCD1602-I2C

nets:
  GND: TP1.GND, TP2.GND, TP3.GND, TP4.GND, TP5.GND, TP6.GND, Part1.GND, Part2.GND
  N1: TP1.I/O, Part1.A2
  VCC: TP1.VCC, TP2.VCC, TP3.VCC, TP4.VCC, TP5.VCC, TP6.VCC, Part1.5V, Part2.VCC
  N2: TP2.I/O, Part1.A1
  N3: TP3.I/O, Part1.A3
  N4: TP4.I/O, Part1.A0
  N5: TP5.I/O, Part1.A5/SCL, Part2.SCL
  N6: TP6.I/O, Part1.A4/SDA, Part2.SDA

custom parts:
  TTP223 Touch Module: Single touch module. Other side has "A" "B" terminal to short and use "AHLB" & "Toggle" Mode.
  TTP223 Touch Module: Single touch module. Other side has "A" "B" terminal to short and use "AHLB" & "Toggle" Mode.
  LCD1602-I2C: A standard character display, usually with 2x16 characters. Comes in many colors with LCM1602 IIC attached.

// code stored in the sketch: Brail keyboard(arduinoo).ino

#include<LiquidCrystal_I2C.h>

LiquidCrystal_I2C lcd(0x27,16,2);

void setup() {
  Serial.begin(115200);
  delay(10); 
 
  pinMode(A0,INPUT);
  pinMode(A1,INPUT);
  pinMode(A2,INPUT);
  pinMode(A3,INPUT);
  pinMode(11,INPUT);
  pinMode(10,INPUT);
  lcd.begin();
  lcd.backlight();
  lcd.clear();
  lcd.setCursor(0,0);
  lcd.print("*Braille**");


  

delay(2000);
}

void loop() {
  
  
  int a= digitalRead(A0); //1
  int b= digitalRead(A1); //1
  int c= digitalRead(A2); //1
  int d= digitalRead(A3); //1
  int e= digitalRead(11); //1
  int f= digitalRead(10); //1

  String s=String(a)+String(b)+String(c)+String(d)+String(e)+String(f);
  //Serial.print(s);

  String A="100000";
  String B="110000";
  String C="100100";
  String D="100110";
  String E="100010";
  String F="110100";
  String G="110110";
  String H="110010";
  String I="010100";
  String J="010110";
  String K="101000";
  String L="111000";
  String M="101100";
  String N="101110";
  String O="101010";
  String P="111100";
  String Q="111110";
  String R="111100";
  String S="011100";
  String T="011110";
  String U="101001";
  String V="111001";
  String W="010111";
  String X="101101";
  String Y="101111";
  String Z="101011";


  if(s==A){
    Serial.print("A");
    lcd.setCursor(0,1);
    lcd.print("A");
    
  }
  else if(s==B){
    Serial.print("B");
    lcd.setCursor(0,1);
    lcd.print("B");
    
  }
  else if(s==C){
    Serial.print("C");
    lcd.setCursor(0,1);
    lcd.print("C");
    
  }
  else if(s==D){
    Serial.print("D");
    lcd.setCursor(0,1);
    lcd.print("D");
    
  }
  else if(s==E){
    Serial.print("E");
    lcd.setCursor(0,1);
    lcd.print("E");
    
  }
  else if(s==F){
    Serial.print("F");
    lcd.setCursor(0,1);
    lcd.print("F");
    
  }
  else if(s==G){
    Serial.print("G");
    lcd.setCursor(0,1);
    lcd.print("G");
    
  }
  else if(s==H){
    Serial.print("H");
    lcd.setCursor(0,1);
    lcd.print("H");
    
  }
  else if(s==I){
    Serial.print("I");
    lcd.setCursor(0,1);
    lcd.print("I");
    
  }
  else if(s==J){
    Serial.print("J");
    lcd.setCursor(0,1);
    lcd.print("J");
    
  }
  else if(s==K){
    Serial.print("K");
    lcd.setCursor(0,1);
    lcd.print("K");
    
  }
  else if(s==L){
    Serial.print("L");
    lcd.setCursor(0,1);
    lcd.print("L");
    
  }
  else if(s==M){
    Serial.print("M");
    lcd.setCursor(0,1);
    lcd.print("M");
    
  }
  else if(s==N){
    Serial.print("N");
    lcd.setCursor(0,1);
    lcd.print("N");
    
  }
  else if(s==O){
    Serial.print("O");
    lcd.setCursor(0,1);
    lcd.print("O");
    
  }
  else if(s==P){
    Serial.print("P");
    lcd.setCursor(0,1);
    lcd.print("P");
    
  }
  else if(s==Q){
    Serial.print("Q");
    lcd.setCursor(0,1);
    lcd.print("Q");
    
  }
  else if(s==R){
    Serial.print("R");
    lcd.setCursor(0,1);
    lcd.print("R");
    
  }
  else if(s==S){
    Serial.print("S");
    lcd.setCursor(0,1);
    lcd.print("S");
    
  }
  else if(s==T){
    Serial.print("T");
    lcd.setCursor(0,1);
    lcd.print("T");
    
  }
  else if(s==U){
    Serial.print("U");
    lcd.setCursor(0,1);
    lcd.print("U");
    
  }
  else if(s==V){
    Serial.print("V");
    lcd.setCursor(0,1);
    lcd.print("V");
    
  }
  else if(s==W){
    Serial.print("W");
    lcd.setCursor(0,1);
    lcd.print("W");
    
  }
  else if(s==X){
    Serial.print("X");
    lcd.setCursor(0,1);
    lcd.print("X");
    
  }
  else if(s==Y){
    Serial.print("Y");
    lcd.setCursor(0,1);
    lcd.print("Y");
    
  }
  else if(s==Z){
    Serial.print("Z");
    lcd.setCursor(0,1);
    lcd.print("Z");
    
  }
  
  delay(250);
}
